# Fritzing sketch schematics (saved by Fritzing 0.9.3b)
circuit board: 13.545cm x 9.58702cm
breadboards: 1

parts:
  Bauteil2 = Arduino Nano (Rev3.0)
  OLED1 = OLED 128x64 I2C Monochrome Display
  XLR1 = XLR3_NCFAH2 [package=xlr3_nc3fah2]
  XLR2 = XLR3_NCFAH2 [package=xlr3_nc3fah2]
  AMPHENOL_-_ACJS-MHDR_-_JACK_6_35MM1 = AMPHENOL - ACJS-MHDR [package=ACJS-MHDR]
  AMPHENOL_-_ACJS-MHDR_-_JACK_6_35MM2 = AMPHENOL - ACJS-MHDR [package=ACJS-MHDR]
  S4 = Pushbutton [package="[THT]"]
  S5 = SWITCH-DPDT [package=gpi-152-3013]
  VCC1 = Battery block 9V
  J1 = female pin header, 4 pins [form="♀ (female)"]
  J2 = female pin header, 4 pins [form="♀ (female)"]
  switch1 = Rotary_Switch_12x1
  D7 = Diode [package=diode-1n4148]
  D8 = Diode [package=diode-1n4148]
  D9 = Diode [package=diode-1n4148]
  D10 = Diode [package=diode-1n4148]

nets (from the breadboard view):
  GND: Bauteil2.GND, OLED1.GND, S4.Pin_3, S4.Pin_4, S5.5, VCC1.-, switch1.0
  N1: Bauteil2.D2, S4.Pin_1, S4.Pin_2
  N2: Bauteil2.D3, D7.C
  N3: Bauteil2.D4, D10.C
  N4: Bauteil2.D5, D8.C
  N5: Bauteil2.D6, D9.C
  N6: Bauteil2.D7, AMPHENOL_-_ACJS-MHDR_-_JACK_6_35MM1.Tip_(6)
  N7: Bauteil2.D8, AMPHENOL_-_ACJS-MHDR_-_JACK_6_35MM1.Ring_(5)
  N8: Bauteil2.D9, AMPHENOL_-_ACJS-MHDR_-_JACK_6_35MM1.Sleeve_(4)
  N9: Bauteil2.D10, J2.pin4
  N10: Bauteil2.D11/MOSI, S5.6
  N11: Bauteil2.D12/MISO, S5.4
  N12: Bauteil2.VIN, S5.1, S5.3
  5V: Bauteil2.5V, OLED1.VDD
  N13: Bauteil2.A5, OLED1.SCK
  N14: Bauteil2.A4, OLED1.SDA
  N15: Bauteil2.A3, switch1.2
  N16: Bauteil2.A2, switch1.1
  N17: Bauteil2.A1, switch1.12
  N18: Bauteil2.A0, switch1.11
  N19: XLR1.1, AMPHENOL_-_ACJS-MHDR_-_JACK_6_35MM1.Sleeve_(1), J2.pin3
  N20: XLR1.2, AMPHENOL_-_ACJS-MHDR_-_JACK_6_35MM1.Ring_(2), J2.pin2
  N21: XLR1.3, AMPHENOL_-_ACJS-MHDR_-_JACK_6_35MM1.Tip_(3), J2.pin1
  N22: XLR2.1, AMPHENOL_-_ACJS-MHDR_-_JACK_6_35MM2.Sleeve_(4), J1.pin3
  N23: XLR2.2, AMPHENOL_-_ACJS-MHDR_-_JACK_6_35MM2.Ring_(5), J1.pin2
  N24: XLR2.3, AMPHENOL_-_ACJS-MHDR_-_JACK_6_35MM2.Tip_(6), J1.pin1
  N25: AMPHENOL_-_ACJS-MHDR_-_JACK_6_35MM2.Sleeve_(1), D10.A
  N26: AMPHENOL_-_ACJS-MHDR_-_JACK_6_35MM2.Ring_(2), D8.A
  N27: AMPHENOL_-_ACJS-MHDR_-_JACK_6_35MM2.Tip_(3), D9.A
  N28: S5.2, VCC1.+
  N29: J1.pin4, D7.A

notes:
  6.35mm
  XLR
  SpeakOn
  Mode Selector
  Mode Selector
  2 Pole ON OFF ON Switch
  Diodes
  Cable Selector
  4 Position Rotary Switch
  Start Button
  In
  Out
